# Fritzing sketch Fritzing_sketch (saved by Fritzing 0.9.6b)

parts:
  Pico = Raspberry Pi Pico H
  A1 = Waveshare e-Paper HAT [package=THT]
  Btn = Arcade Button (white)
  LED1 = LEDs [package=led10mm]
  Sw1 = Momentary Switch [package=ksa_sealed_tac_switch]
  R1 = Resistor [tolerance=±5% resistance=220 package="2010 [SMD]"]
  Sw2 = Momentary Switch [package=ksa_sealed_tac_switch]
  Sw3 = Momentary Switch [package=ksa_sealed_tac_switch]
  Printer_TTY = JST-B3P-VH [part_number=JST-B3P-VH package=THT]
  Printer_Pwr = JST-B3P-VH [part_number=JST-B3P-VH package=THT]
  A2 = Mini RS232 to ttl module

nets (from the breadboard view):
  N1: Pico.VBUS, Printer_Pwr.pin3
  N2: Pico.VSYS, A1.pin_8, A2.Pin_6
  N3: Pico.GND, A1.pin_7, LED1.C, Printer_Pwr.pin1, A2.Pin_1, A2.Pin_5
  N4: Pico.3V3, Btn.no_name_yet#1, Sw1.1, Sw2.1, Sw3.1
  N5: Pico.GP20, Sw1.2
  N6: Pico.GP19, Sw2.2
  N7: Pico.GP18, Sw3.2
  N8: Pico.GP17, Btn.no_name_yet#2
  N9: Pico.GP16, R1.Pin_1
  N10: Pico.GP13, A1.pin_1
  N11: Pico.GP12, A1.pin_2
  N12: Pico.GP11, A1.pin_6
  N13: Pico.GP10, A1.pin_5
  N14: Pico.GP9, A1.pin_4
  N15: Pico.GP8, A1.pin_3
  N16: Pico.GP2, Printer_TTY.pin3
  N17: Pico.GP1, A2.Pin_8
  N18: Pico.GP0, A2.Pin_7
  N19: LED1.A, R1.Pin_0
  N20: Printer_TTY.pin2, A2.Pin_4
  N21: Printer_TTY.pin1, A2.Pin_3

notes:
  Printer RS232
  Printer Power
  Arcade LED Button
  Raspberry Pi Pico
  Waveshare e-Paper Hat
  Tactile Button Array
  RS232<->TTL

custom parts:
  Raspberry Pi Pico H: Raspberry Pi Pico H. Based around the RP2040 microcontroller the Pico H is a low cost microcontroller device bringing Raspberry Pi quality, cost, and easy of use to the microcontroller space.
  Waveshare e-Paper HAT: .This is a universal driver board for e-Paper raw panels, can be used to drive various SPI interface e-Paper from Waveshare.
  Arcade Button (white): Adafruit Arcade Button (white)
  Mini RS232 to ttl module: Mini RS232 to ttl module.
